# Fritzing sketch IR_sketch (saved by Fritzing 0.9.3b)
breadboards: 2

parts:
  WeMos_D1_R1 = WeMos D1 R2
  LED1 = LED - 5mm [color="Green (565nm)" package="5 mm [THT]"]
  LED2 = LED - 5mm [color="Red (633nm)" package="5 mm [THT]"]
  LED3 = LED - 3mm [color="Infrared (940nm)" package="3 mm [THT]"]
  R1 = Resistor [tolerance=±5% resistance=330 package="0603 [SMD]"]
  LED4 = LED - 3mm [color="Infrared (850nm)" package="3 mm [THT]"]
  R2 = Resistor [tolerance=±5% resistance=330 package="0603 [SMD]"]

nets:
  N1: WeMos_D1_R1.D0/RX, WeMos_D1_R1.A0, R1.Pin_0
  N2: WeMos_D1_R1.(D6), LED2.anode
  N3: WeMos_D1_R1.(D7), LED1.anode
  N4: WeMos_D1_R1.GND, LED1.cathode, LED2.cathode, LED3.anode, R2.Pin_1
  N5: WeMos_D1_R1.3.3V, LED4.anode
  N6: LED3.cathode, R1.Pin_1
  N7: LED4.cathode, R2.Pin_0

custom parts:
  WeMos D1 R2: The D1 R2 is a mini wifi board based on the ESP-8266EX.
