# Fritzing sketch LDR_fritzing (saved by Fritzing 0.9.3b)
breadboards: 1

parts:
  WeMos_D1_R1 = WeMos D1 R2
  LED1 = LED - 5mm [color="White (6500K)" package="5 mm [THT]"]
  LED2 = LED - 5mm [color="White (6500K)" package="5 mm [THT]"]
  R1 = Photocell (LDR) [package=THT]
  R2 = Resistor [tolerance=±5% resistance=220 package=THT]
  LED3 = LED - 5mm [color="White (6500K)" package="5 mm [THT]"]

nets:
  N1: WeMos_D1_R1.(D6), LED3.cathode
  N2: WeMos_D1_R1.(D7), LED2.cathode
  N3: WeMos_D1_R1.D8, LED1.cathode
  N4: WeMos_D1_R1.GND, R2.Pin_1
  N5: WeMos_D1_R1.A0, R1.pin_1, R2.Pin_0
  N6: WeMos_D1_R1.5V, LED1.anode, LED2.anode, R1.pin_0, LED3.anode

custom parts:
  WeMos D1 R2: The D1 R2 is a mini wifi board based on the ESP-8266EX.
