# Fritzing sketch Servo_fritzing (saved by Fritzing 0.9.3b)
breadboards: 1

parts:
  WeMos_D1_R1 = WeMos D1 R2
  R1 = Resistor [tolerance=±5% resistance=330 package=THT]
  S1 = Pushbutton [package="[THT]"]
  J1 = Basic Servo

nets:
  N1: WeMos_D1_R1.(D7), R1.Pin_0, S1.Pin_3, S1.Pin_4
  GND: WeMos_D1_R1.GND, R1.Pin_1, J1.gnd
  5V: WeMos_D1_R1.5V, S1.Pin_1, S1.Pin_2, J1.vcc

custom parts:
  WeMos D1 R2: The D1 R2 is a mini wifi board based on the ESP-8266EX.
