# Fritzing sketch Ultrasound_fritzing (saved by Fritzing 0.9.3b)
breadboards: 1

parts:
  WeMos_D1_R1 = WeMos D1 R2
  hc-sr1 = hc-sr04
  LED1 = LED - 5mm [color="Red (633nm)" package="5 mm [THT]"]
  LED2 = LED - 5mm [color="Yellow (585nm)" package="5 mm [THT]"]
  LED3 = LED - 5mm [color="Green (555nm)" package="5 mm [THT]"]
  R1 = Resistor [tolerance=±5% resistance=330 package=THT]
  R2 = Resistor [tolerance=±5% resistance=330 package=THT]
  R3 = Resistor [tolerance=±5% resistance=330 package=THT]

nets:
  N1: WeMos_D1_R1.(D6), LED3.anode
  N2: WeMos_D1_R1.(D7), LED2.anode
  N3: WeMos_D1_R1.D8, LED1.anode
  N4: WeMos_D1_R1.GND#15, R1.Pin_1, R3.Pin_1
  N5: WeMos_D1_R1.D14, hc-sr1.Echo
  N6: WeMos_D1_R1.D15, hc-sr1.Trig
  N7: WeMos_D1_R1.GND#21, hc-sr1.GND
  5V: WeMos_D1_R1.5V, hc-sr1.VCC
  N8: LED1.cathode, R1.Pin_0
  N9: LED2.cathode, R2.Pin_0
  N10: LED3.cathode, R3.Pin_0

custom parts:
  WeMos D1 R2: The D1 R2 is a mini wifi board based on the ESP-8266EX.
