# Fritzing sketch Water_sensor_fritzing (saved by Fritzing 0.9.3b)
breadboards: 1

parts:
  LED1 = LED - 5mm [color="Green (565nm)" package="5 mm [THT]"]
  LED2 = LED - 5mm [color="Yellow (592nm)" package="5 mm [THT]"]
  LED3 = LED - 5mm [color="Red (633nm)" package="5 mm [THT]"]
  R1 = Resistor [tolerance=±5% resistance=330 package=THT]
  R2 = Resistor [tolerance=±5% resistance=330 package=THT]
  R3 = Resistor [tolerance=±5% resistance=330 package=THT]
  WeMos_D1_R1 = WeMos D1 R2
  Water_Level_Sensor1 = Water Level Sensor

nets:
  N1: LED1.cathode, R1.Pin_1
  N2: LED1.anode, LED2.anode, LED3.anode, WeMos_D1_R1.5V#25
  N3: LED2.cathode, R2.Pin_1
  N4: LED3.cathode, R3.Pin_1
  N5: R1.Pin_0, WeMos_D1_R1.D8
  N6: R2.Pin_0, WeMos_D1_R1.(D7)
  N7: R3.Pin_0, WeMos_D1_R1.(D6)
  N8: WeMos_D1_R1.A0, Water_Level_Sensor1.SIG
  GND: WeMos_D1_R1.GND, Water_Level_Sensor1.GND
  N9: WeMos_D1_R1.5V#22, Water_Level_Sensor1.VCC

custom parts:
  WeMos D1 R2: The D1 R2 is a mini wifi board based on the ESP-8266EX.
  Water Level Sensor: A water level sensor. This sensor operates at 3V to 5V. The Sig (signal) pin outputs an analogue signal that is in proportion to the amount of water in contact with the sensor.
